# Fritzing sketch MBU_1 (saved by Fritzing 0.9.3b)
breadboards: 1

parts:
  Part1 = Arduino Uno (Rev3)
  Part2 = Bluetooth HC-05 Macho
  hc-sr1 = hc-sr04
  VCC1 = 4 x AAA Battery Mount
  J1 = Basic Servo

nets:
  N1: Part1.D11_PWM/MOSI, hc-sr1.Echo
  N2: Part1.D12/MISO, hc-sr1.GND
  N3: Part1.D0/RX, Part2.TXD
  N4: Part1.D1/TX, Part2.RXD
  VCC: Part1.5V, Part2.VCC, hc-sr1.VCC
  GND: Part1.GND, Part2.GND, hc-sr1.Trig
  N5: VCC1.-, J1.gnd
  N6: VCC1.+, J1.vcc

// code stored in the sketch: code_1.ino
#include <Servo.h>

int trigPin = 11;
int echoPin = 12;
int pos     = 0;
long duration, cm;

//Bluetooth
String data;

Servo tap;

void setup() {
  
  Serial.begin(9600);

  tap.attach(9);

  //Setting Pins
  //Ultrasom
  pinMode(trigPin, OUTPUT);
  pinMode(echoPin, INPUT);
}

void loop() {
  
  // The sensor is triggered by a HIGH pulse of 10 or more microseconds.
  // Give a short LOW pulse beforehand to ensure a clean HIGH pulse:
  digitalWrite(trigPin, LOW);
  delayMicroseconds(5);
  digitalWrite(trigPin, HIGH);
  delayMicroseconds(10);
  digitalWrite(trigPin, LOW);

  // Read the signal from the sensor: a HIGH pulse whose
  // duration is the time (in microseconds) from the sending
  // of the ping to the reception of its echo off of an object.
  pinMode(echoPin, INPUT);
  duration = pulseIn(echoPin, HIGH);
 
  // convert the time into a distance
  cm = (duration/2) / 29.1;

  if(cm < 20){
    Serial.println(data);
    tap.write(180);
//
//    data="";
//   tap.write(180);
//    Serial.println("Estado critico");
//    Serial.print(cm); 
//    Serial.print("cm\n");
    data = "";
  }
  else{  
    tap.write(0);
  }

  while(Serial.available()){
    delay(20); //small time to fill the buffer

    char c = Serial.read();
    if(c == 'a'){
      tap.write(180);
      delay(700); 
    }
    if(c == ','){
      break;  
    }

    data += c;
         
    //data[0] = Serial.read();
//    tap.write(180);
//    Serial.print(data);
//    Serial.print("\n");
//    delay(1000);
//    Serial.flush();
//    data = "";
  }

//  if(data.length() > 0){
//    Serial.println(data);
//
//    data="";
//  }
  
}

//https://randomnerdtutorials.com/complete-guide-for-ultrasonic-sensor-hc-sr04/
